# Fritzing sketch dice_schematic (saved by Fritzing 0.9.2b)
circuit board: 8.46667cm x 5.64444cm
breadboards: 1

parts:
  S1 = Pushbutton [package="[THT]"]
  R1 = Resistor [tolerance=±5% resistance=1M package=THT]
  LED7 = LED - 5mm [color="Red (633nm)" package="5 mm [THT]"]
  LED3 = LED - 5mm [color="Red (633nm)" package="5 mm [THT]"]
  LED5 = LED - 5mm [color="Red (633nm)" package="5 mm [THT]"]
  LED1 = LED - 5mm [color="Red (633nm)" package="5 mm [THT]"]
  LED4 = LED - 5mm [color="Red (633nm)" package="5 mm [THT]"]
  LED2 = LED - 5mm [color="Red (633nm)" package="5 mm [THT]"]
  POWER = LED - 5mm [color="Yellow (585nm)" package="5 mm [THT]"]
  J1 = Piezo Speaker
  Bauteil1 = Arduino Uno (Rev3)
  LED6 = LED - 5mm [color="Red (633nm)" package="5 mm [THT]"]

nets:
  N1: S1.Pin_1, S1.Pin_2, LED7.cathode, LED3.cathode, LED5.cathode, LED1.cathode, LED4.cathode, LED2.cathode, POWER.cathode, J1.pin1, Bauteil1.GND, LED6.cathode
  N2: S1.Pin_3, S1.Pin_4, R1.Pin_1, Bauteil1.D11_PWM/MOSI
  N3: R1.Pin_0, Bauteil1.5V
  N4: LED7.anode, Bauteil1.D8
  N5: LED3.anode, Bauteil1.D4
  N6: LED5.anode, Bauteil1.D6_PWM
  N7: LED1.anode, Bauteil1.D2
  N8: LED4.anode, Bauteil1.D7
  N9: LED2.anode, Bauteil1.D3_PWM
  N10: POWER.anode, Bauteil1.D5_PWM
  N11: J1.pin2, Bauteil1.D12/MISO
  N12: Bauteil1.D9_PWM, LED6.anode
